# Fritzing sketch ProjectDiagram (saved by Fritzing 0.9.3b)
breadboards: 1

parts:
  S1 = Pushbutton [package="[THT]"]
  LED1 = RGB LED (com. cathode, rgb) [package="5 mm [THT]"]
  S2 = Momentary Switch [package=ksa_sealed_tac_switch]
  S3 = Momentary Switch [package=ksa_sealed_tac_switch]
  LED2 = RGB LED (com. cathode, rgb) [package="5 mm [THT]"]
  LED3 = RGB LED (com. cathode, rgb) [package="5 mm [THT]"]

nets:
  N1: S1.Pin_1, S1.Pin_2, S1.Pin_3, S1.Pin_4, S2.1, S2.3, S3.1, S3.3
  N2: LED1.common_cathode, LED2.common_cathode, LED3.common_cathode
  N3: S2.2, S2.4
  N4: S3.2, S3.4
